# Fritzing sketch MIDI Control Surface 2 (saved by Fritzing 0.8.0b)
breadboards: 1

parts:
  Arduino = Arduino Uno (Rev3)
  HCF_1 = HCF 4067 [package="DIP24 [THT]"]
  HCF_2 = HCF 4067 [package="DIP24 [THT]"]
  R1 = Rotary Potentiometer (Large) [maximum_resistance=100kΩ package=THT]
  R2 = Rotary Potentiometer (Large) [maximum_resistance=100kΩ package=THT]
  R3 = Rotary Potentiometer (Large) [maximum_resistance=100kΩ package=THT]
  R5 = Rotary Potentiometer (Large) [maximum_resistance=100kΩ package=THT]
  R2_2 = Rotary Potentiometer (Large) [maximum_resistance=100kΩ package=THT]
  R6 = Rotary Potentiometer (Large) [maximum_resistance=100kΩ package=THT]
  R7 = Rotary Potentiometer (Large) [maximum_resistance=100kΩ package=THT]
  R8 = Rotary Potentiometer (Large) [maximum_resistance=100kΩ package=THT]
  R9 = Rotary Potentiometer (Large) [maximum_resistance=100kΩ package=THT]
  R10 = Rotary Potentiometer (Large) [maximum_resistance=100kΩ package=THT]
  R11 = Rotary Potentiometer (Large) [maximum_resistance=100kΩ package=THT]
  R12 = Rotary Potentiometer (Large) [maximum_resistance=100kΩ package=THT]
  R13 = Rotary Potentiometer (Large) [maximum_resistance=100kΩ package=THT]
  R14 = Rotary Potentiometer (Large) [maximum_resistance=100kΩ package=THT]
  R15 = Rotary Potentiometer (Large) [maximum_resistance=100kΩ package=THT]
  R16 = Rotary Potentiometer (Large) [maximum_resistance=100kΩ package=THT]
  R17 = Rotary Potentiometer (Large) [maximum_resistance=100kΩ package=THT]
  R18 = Rotary Potentiometer (Large) [maximum_resistance=100kΩ package=THT]
  R19 = Rotary Potentiometer (Large) [maximum_resistance=100kΩ package=THT]
  R20 = Rotary Potentiometer (Large) [maximum_resistance=100kΩ package=THT]
  S1 = Round Pushbutton
  S2 = Round Pushbutton
  S3 = Round Pushbutton
  S4 = Round Pushbutton
  S5 = Round Pushbutton
  S6 = Round Pushbutton
  S7 = Round Pushbutton
  S8 = Round Pushbutton
  S9 = Round Pushbutton
  S10 = Round Pushbutton
  S11 = Round Pushbutton
  S12 = Round Pushbutton
  S13 = Round Pushbutton
  S14 = Round Pushbutton
  S15 = Round Pushbutton
  S16 = Round Pushbutton
  S17 = Round Pushbutton
  R21 = Resistor [tolerance=±5% resistance=10k package=THT]
  R22 = Resistor [tolerance=±5% resistance=10 package=THT]
  R23 = Resistor [tolerance=±5% resistance=10k package=THT]
  R24 = Resistor [tolerance=±5% resistance=10k package=THT]
  R25 = Resistor [tolerance=±5% resistance=10k package=THT]
  R26 = Resistor [tolerance=±5% resistance=10k package=THT]
  R27 = Resistor [tolerance=±5% resistance=10k package=THT]
  R28 = Resistor [tolerance=±5% resistance=10k package=THT]
  R29 = Resistor [tolerance=±5% resistance=10k package=THT]
  R30 = Resistor [tolerance=±5% resistance=10k package=THT]
  R31 = Resistor [tolerance=±5% resistance=10k package=THT]
  R32 = Resistor [tolerance=±5% resistance=10k package=THT]
  R33 = Resistor [tolerance=±5% resistance=10k package=THT]
  R34 = Resistor [tolerance=±5% resistance=10k package=THT]
  R35 = Resistor [tolerance=±5% resistance=10k package=THT]
  R36 = Resistor [tolerance=±5% resistance=10k package=THT]
  R37 = Resistor [tolerance=±5% resistance=10k package=THT]

nets:
  N1: Arduino.A0, HCF_1.1_O/I
  N2: Arduino.A1, R20.wiper
  N3: Arduino.A2, R19.wiper
  N4: Arduino.A3, R18.wiper
  N5: Arduino.A4/SDA, R17.wiper
  N6: Arduino.5V, HCF_1.24_Vdd, HCF_2.24_Vdd, R1.leg1, R2.leg1, R3.leg1, R5.leg1, R2_2.leg1, R6.leg1, R7.leg1, R8.leg1, R9.leg1, R10.leg1, R11.leg1, R12.leg1, R13.leg1, R14.leg1, R15.leg1, R16.leg1, R17.leg1, R18.leg1, R19.leg1, R20.leg1, S1.leg0, S2.leg0, S3.leg0, S4.leg0, S5.leg0, S6.leg0, S7.leg0, S8.leg0, S9.leg0, S10.leg0, S11.leg0, S12.leg0, S13.leg0, S14.leg0, S15.leg0, S16.leg0, S17.leg0
  N7: Arduino.GND, HCF_1.12_VSS, HCF_1.15_Inhibit, HCF_2.12_VSS, HCF_2.15_Inhibit, R1.leg2, R2.leg2, R3.leg2, R5.leg2, R2_2.leg2, R6.leg2, R7.leg2, R8.leg2, R9.leg2, R10.leg2, R11.leg2, R12.leg2, R13.leg2, R14.leg2, R15.leg2, R16.leg2, R17.leg2, R18.leg2, R19.leg2, R20.leg2, R21.Pin_1, R22.Pin_1, R23.Pin_1, R24.Pin_1, R25.Pin_1, R26.Pin_1, R27.Pin_1, R28.Pin_1, R29.Pin_1, R30.Pin_1, R31.Pin_1, R32.Pin_1, R33.Pin_1, R34.Pin_1, R35.Pin_1, R36.Pin_1, R37.Pin_1
  N8: Arduino.D2, HCF_1.13_D, HCF_2.13_D
  N9: Arduino.D3_PWM, HCF_1.14_C, HCF_2.14_C
  N10: Arduino.D4, HCF_1.11_B, HCF_2.11_B
  N11: Arduino.D5_PWM, HCF_1.10_A, HCF_2.10_A
  N12: Arduino.D6_PWM, HCF_2.1_O/I
  N13: Arduino.D7, S17.leg1, R37.Pin_0
  N14: HCF_1.2_TG_7, R9.wiper
  N15: HCF_1.3_TG6, R10.wiper
  N16: HCF_1.4_TG5, R11.wiper
  N17: HCF_1.5_TG4, R12.wiper
  N18: HCF_1.6_TG3, R13.wiper
  N19: HCF_1.7_TG2, R14.wiper
  N20: HCF_1.8_TG1, R15.wiper
  N21: HCF_1.9_TG0, R16.wiper
  N22: HCF_1.16_TG15, R1.wiper
  N23: HCF_1.17_TG14, R2_2.wiper
  N24: HCF_1.18_TG13, R3.wiper
  N25: HCF_1.19_TG12, R2.wiper
  N26: HCF_1.20_TG11, R5.wiper
  N27: HCF_1.21_TG10, R6.wiper
  N28: HCF_1.22_TG9, R7.wiper
  N29: HCF_1.23_TG8, R8.wiper
  N30: HCF_2.2_TG_7, S9.leg1, R29.Pin_0
  N31: HCF_2.3_TG6, S10.leg1, R30.Pin_0
  N32: HCF_2.4_TG5, S11.leg1, R31.Pin_0
  N33: HCF_2.5_TG4, S12.leg1, R32.Pin_0
  N34: HCF_2.6_TG3, S13.leg1, R33.Pin_0
  N35: HCF_2.7_TG2, S14.leg1, R34.Pin_0
  N36: HCF_2.8_TG1, S15.leg1, R35.Pin_0
  N37: HCF_2.9_TG0, S16.leg1, R36.Pin_0
  N38: HCF_2.16_TG15, S1.leg1, R21.Pin_0
  N39: HCF_2.17_TG14, S2.leg1, R22.Pin_0
  N40: HCF_2.18_TG13, S3.leg1, R23.Pin_0
  N41: HCF_2.19_TG12, S4.leg1, R24.Pin_0
  N42: HCF_2.20_TG11, S5.leg1, R25.Pin_0
  N43: HCF_2.21_TG10, S6.leg1, R26.Pin_0
  N44: HCF_2.22_TG9, S7.leg1, R27.Pin_0
  N45: HCF_2.23_TG8, S8.leg1, R28.Pin_0
