# Fritzing sketch MIDI Control Surface (saved by Fritzing 0.8.0b)
breadboards: 6

parts:
  R1 = Rotary Potentiometer (Large) [maximum_resistance=100kΩ package=THT]
  R2 = Rotary Potentiometer (Large) [maximum_resistance=100kΩ package=THT]
  R3 = Rotary Potentiometer (Large) [maximum_resistance=100kΩ package=THT]
  R4 = Rotary Potentiometer (Large) [maximum_resistance=100kΩ package=THT]
  S1 = Round Pushbutton  # not connected
  S2 = Round Pushbutton  # not connected
  R5 = Rotary Potentiometer (Large) [maximum_resistance=100kΩ package=THT]
  R6 = Rotary Potentiometer (Large) [maximum_resistance=100kΩ package=THT]
  R7 = Rotary Potentiometer (Large) [maximum_resistance=100kΩ package=THT]
  R8 = Rotary Potentiometer (Large) [maximum_resistance=100kΩ package=THT]
  S3 = Round Pushbutton  # not connected
  S4 = Round Pushbutton  # not connected
  R9 = Rotary Potentiometer (Large) [maximum_resistance=100kΩ package=THT]
  R10 = Rotary Potentiometer (Large) [maximum_resistance=100kΩ package=THT]
  R11 = Rotary Potentiometer (Large) [maximum_resistance=100kΩ package=THT]
  R12 = Rotary Potentiometer (Large) [maximum_resistance=100kΩ package=THT]
  S5 = Round Pushbutton  # not connected
  S6 = Round Pushbutton  # not connected
  R13 = Rotary Potentiometer (Large) [maximum_resistance=100kΩ package=THT]
  R14 = Rotary Potentiometer (Large) [maximum_resistance=100kΩ package=THT]
  R15 = Rotary Potentiometer (Large) [maximum_resistance=100kΩ package=THT]
  R16 = Rotary Potentiometer (Large) [maximum_resistance=100kΩ package=THT]
  S7 = Round Pushbutton  # not connected
  S8 = Round Pushbutton  # not connected
  R17 = Rotary Potentiometer (Large) [maximum_resistance=100kΩ package=THT]
  R18 = Rotary Potentiometer (Large) [maximum_resistance=100kΩ package=THT]
  R19 = Rotary Potentiometer (Large) [maximum_resistance=100kΩ package=THT]
  R20 = Rotary Potentiometer (Large) [maximum_resistance=100kΩ package=THT]
  S9 = Round Pushbutton  # not connected
  S10 = Round Pushbutton  # not connected
  S11 = Round Pushbutton  # not connected
  S12 = Round Pushbutton  # not connected
  S13 = Round Pushbutton  # not connected
  S14 = Round Pushbutton  # not connected
  S15 = Round Pushbutton  # not connected
  S16 = Round Pushbutton  # not connected
  S18 = Round Pushbutton  # not connected
  HCF_1 = HCF 4067 [package="DIP24 [THT]"]
  Part1 = Arduino Uno (Rev3)
  HCF_3 = HCF 4067 [package="DIP24 [THT]"]
  HCF_5 = HCF 4067 [package="DIP24 [THT]"]

nets:
  N1: R1.leg1, R2.leg1, R3.leg1, R4.leg1, R5.leg1, R6.leg1, R7.leg1, R8.leg1, R9.leg1, R10.leg1, R11.leg1, R12.leg1, R13.leg1, R14.leg1, R15.leg1, R16.leg1, R17.leg1, R18.leg1, R19.leg1, R20.leg1, HCF_1.24_Vdd, Part1.5V, HCF_3.24_Vdd, HCF_5.24_Vdd
  N2: R1.wiper, HCF_1.4_TG5
  N3: R1.leg2, R2.leg2, R3.leg2, R4.leg2, R5.leg2, R6.leg2, R7.leg2, R8.leg2, R9.leg2, R10.leg2, R11.leg2, R12.leg2, R13.leg2, R14.leg2, R15.leg2, R16.leg2, R17.leg2, R18.leg2, R19.leg2, R20.leg2, HCF_1.12_VSS, HCF_1.15_Inhibit, Part1.GND, HCF_3.12_VSS, HCF_3.15_Inhibit, HCF_5.12_VSS
  N4: R2.wiper, HCF_1.5_TG4
  N5: R3.wiper, HCF_1.6_TG3
  N6: R4.wiper, HCF_1.7_TG2
  N7: R5.wiper, HCF_1.20_TG11
  N8: R6.wiper, HCF_1.21_TG10
  N9: R7.wiper, HCF_1.22_TG9
  N10: R8.wiper, HCF_1.23_TG8
  N11: R9.wiper, HCF_3.4_TG5
  N12: R10.wiper, HCF_3.5_TG4
  N13: R11.wiper, HCF_3.6_TG3
  N14: R12.wiper, HCF_3.7_TG2
  N15: R13.wiper, HCF_3.20_TG11
  N16: R14.wiper, HCF_3.21_TG10
  N17: R15.wiper, HCF_3.22_TG9
  N18: R16.wiper, HCF_3.23_TG8
  N19: R17.wiper, HCF_5.4_TG5
  N20: R18.wiper, HCF_5.5_TG4
  N21: R19.wiper, HCF_5.6_TG3
  N22: R20.wiper, HCF_5.7_TG2
  N23: HCF_1.1_O/I, Part1.A0
  N24: HCF_1.10_A, Part1.D5_PWM
  N25: HCF_1.11_B, Part1.D4
  N26: HCF_1.13_D, Part1.D2
  N27: HCF_1.14_C, Part1.D3_PWM
  N28: Part1.A1, HCF_3.1_O/I
  N29: Part1.A2, HCF_5.1_O/I
  N30: Part1.ICSP_MISO, Part1.D12/MISO, HCF_5.11_B
  N31: Part1.ICSP_SCK, Part1.D13/SCK, HCF_5.10_A
  N32: Part1.D8, HCF_3.11_B
  N33: Part1.D9_PWM, HCF_3.10_A
  N34: Part1.D10_PWM/SS, HCF_5.13_D
  N35: Part1.D11_PWM/MOSI, HCF_5.14_C
  N36: Part1.D6_PWM, HCF_3.13_D
  N37: Part1.D7, HCF_3.14_C
